# Fritzing sketch breadboard (saved by Fritzing 0.9.4)
breadboards: 5

parts:
  Part1 = Arduino Uno (Rev3) - ICSP
  Raspberry_Pi1 = Raspberry Pi B+  # not connected
  J1 = Raspberry Pi Header 40pin [form="♂ (male)" package=THT]  # not connected
  INA1 = INA219 DC Current Sensor Breakout
  INA2 = INA219 DC Current Sensor Breakout
  INA3 = INA219 DC Current Sensor Breakout
  INA4 = INA219 DC Current Sensor Breakout
  Part2 = RFID-RC522-v2
  LED1 = LED - 3mm [color="White (6500K)" package="3 mm [THT]"]
  LED2 = LED - 3mm [color="White (6500K)" package="3 mm [THT]"]
  D1 = Diode [package=diode-1n4148]
  M1 = DC Motor
  Q1 = NPN-Transistor [package="SOT-23 [SMD]"]
  R1 = Resistor [tolerance=±5% resistance=470 package="0402 [SMD]"]
  R2 = Resistor [tolerance=±5% resistance=10 package="0402 [SMD]"]
  R5 = Resistor [tolerance=±5% resistance=10 package="0402 [SMD]"]
  Q2 = NPN-Transistor [package="SOT-23 [SMD]"]
  R6 = Resistor [tolerance=±5% resistance=470 package="0402 [SMD]"]
  Q3 = npn-Powertransistor [package="TO220 [THT]"]
  R7 = Resistor [tolerance=±5% resistance=5.1k package="0402 [SMD]"]
  D2 = Diode [package=diode-1n4148]
  L1 = Solenoid
  LCD1 = LCD screen  # not connected
  INA5 = INA219 DC Current Sensor Breakout  # not connected
  INA6 = INA219 DC Current Sensor Breakout  # not connected
  R8 = Resistor [tolerance=±5% resistance=100 package="0402 [SMD]"]
  R9 = Resistor [tolerance=±5% resistance=100 package="0402 [SMD]"]
  Q4 = NPN-Transistor [package="SOT-23 [SMD]"]
  R10 = Resistor [tolerance=±5% resistance=100 package="0402 [SMD]"]
  LED3 = LED - 3mm [color="White (6500K)" package="3 mm [THT]"]
  R11 = Resistor [tolerance=±5% resistance=100 package="0402 [SMD]"]
  LED4 = LED - 3mm [color="White (6500K)" package="3 mm [THT]"]
  R12 = Resistor [tolerance=±5% resistance=100 package="0402 [SMD]"]
  Q5 = NPN-Transistor [package="SOT-23 [SMD]"]
  R13 = Resistor [tolerance=±5% resistance=100 package="0402 [SMD]"]
  LED5 = LED - 3mm [color="White (6500K)" package="3 mm [THT]"]
  R14 = Resistor [tolerance=±5% resistance=100 package="0402 [SMD]"]
  LED6 = LED - 3mm [color="White (6500K)" package="3 mm [THT]"]
  R15 = Resistor [tolerance=±5% resistance=100 package="0402 [SMD]"]
  Q6 = NPN-Transistor [package="SOT-23 [SMD]"]
  R16 = Resistor [tolerance=±5% resistance=100 package="0402 [SMD]"]
  Part3 = I2C level shifter bidirectional
  IR1 = TSOP312.., 314.. [package=THT]
  R17 = TRIMPOT [package=trimpot_pth_s3_lock]
  DS1 = DS18B20 1-Wire Temperature Sensor [part_number=DS18B20]
  R18 = Resistor [tolerance=±5% resistance=4.7k package="0402 [SMD]"]
  ADC1 = MCP3008 [package=dil16]
  U1 = PCF8574 [package="DIP16 [THT]"]  # not connected
  S1 = Pushbutton [package="[SMD]"]
  R19 = Resistor [tolerance=±5% resistance=100 package="0402 [SMD]"]
  S2 = TILT-SWITCH-SW-200D [package=reed_switch_plastic]
  R20 = Resistor [tolerance=±5% resistance=100 package="0402 [SMD]"]
  R21 = Photocell (LDR) [package=THT]
  R22 = Resistor [tolerance=±5% resistance=10k package="0402 [SMD]"]

nets:
  N1: Part1.D0/RX, Part3.HV1
  VCC: INA1.VCC, INA1.Vin+, INA2.VCC, INA2.Vin+, DS1.VDD
  GND: INA1.GND, INA2.GND, INA3.GND, INA4.GND, DS1.GND
  N2: INA1.Vin-, LED1.anode, LED2.anode
  N3: INA2.SCL, INA3.SCL, INA4.SCL
  N4: INA2.SDA, INA3.SDA, INA4.SDA
  N5: INA2.Vin-, LED3.cathode, R11.Pin_0
  VCC_2: INA3.VCC, INA4.VCC
  N6: INA3.Vin-, D1.C, M1.pin_1
  N7: INA3.Vin+, INA4.Vin+
  N8: INA4.Vin-, R2.Pin_0, R5.Pin_0
  N9: Part2.GND, Q4.2, Q5.2, Q6.2, S1.Pin_1, S1.Pin_2, S1.Pin_3, S1.Pin_4, R19.Pin_0, S2.1
  N10: Part2.3.3V, LED5.cathode, R14.Pin_0, R19.Pin_1, R20.Pin_1
  N11: LED1.cathode, R9.Pin_0
  N12: LED2.cathode, R8.Pin_0
  N13: D1.A, M1.pin_2, Q1.1
  N14: Q1.2, Q2.2, IR1.GND
  N15: Q1.0, R1.Pin_0
  N16: R2.Pin_1, R5.Pin_1, Q2.1
  N17: Q2.0, R6.Pin_0
  N18: Q3.base, R7.Pin_1
  N19: Q3.collector, L1.pin1
  N20: D2.C, L1.pin2, IR1.Vs
  N21: R8.Pin_1, R9.Pin_1, Q4.1
  N22: Q4.0, R10.Pin_1
  N23: LED3.anode, LED4.anode
  N24: R11.Pin_1, R12.Pin_1, Q5.1
  N25: LED4.cathode, R12.Pin_0
  N26: Q5.0, R13.Pin_1
  N27: LED5.anode, LED6.anode
  N28: R14.Pin_1, R15.Pin_1, Q6.1
  N29: LED6.cathode, R15.Pin_0
  N30: Q6.0, R16.Pin_1
  N31: R17.CCW, R21.pin_1
  N32: R17.WIPER, ADC1.CH0
  N33: R17.CW, R22.Pin_0
  N34: DS1.DQ, R18.Pin_1
  N35: ADC1.CH1, R21.pin_0, R22.Pin_1
  N36: ADC1.DGND, ADC1.AGND
  N37: ADC1.VREF, ADC1.VDD
  N38: S2.2, R20.Pin_0

custom parts:
  Raspberry Pi Header 40pin: Raspberry Pi 40 pin header - for creating your own shields.
  INA219 DC Current Sensor Breakout: INA DC Current Sensor Breakout
  RFID-RC522-v2: A simple China made RFID-RC522 Reader; do check the pin labels, as this is a MFRC522 based clone.
