# Fritzing sketch schematic (saved by Fritzing 0.9.4)
breadboards: 1

parts:
  Raspberry_Pi_5_8GB = Raspberry Pi B+
  MCP3008 = MCP3008 [package=dil16]
  IR1 = TSOP312.., 314.. [package=THT]
  Solar_panel = SOLAR-IXYS [package=solarbit-12x1]
  Powerbank_OUTPUT_5V = BC9VPC [package=bc9vpc]
  INA1 = INA219 DC Current Sensor Breakout
  RFID = RFID-RC522-v2
  LED1 = LEDs [package=led10mm]
  LED2 = LEDs [package=led10mm]
  LED4 = LEDs [package=led10mm]
  LED_3 = LEDs [package=led10mm]
  M1 = DC Motor
  INA2 = INA219 DC Current Sensor Breakout
  INA3 = INA219 DC Current Sensor Breakout
  INA4 = INA219 DC Current Sensor Breakout
  R7/Heating_pad = Resistor [tolerance=±5% resistance=10 package="2512 [SMD]"]
  Q1_SS8050 = TRANSISTOR_NPN [package=to-92]
  Q2_SS8050 = TRANSISTOR_NPN [package=to-92]
  5V_TO_3V3 = Transformer [package=transformer_smd]
  R6 = Resistor [tolerance=±5% resistance=470 package="2512 [SMD]"]
  R5 = Resistor [tolerance=±5% resistance=470 package="2512 [SMD]"]
  R1 = Resistor [tolerance=±5% resistance=100 package="0805 [SMD]"]
  R3 = Resistor [tolerance=±5% resistance=100 package="0805 [SMD]"]
  R2 = Resistor [tolerance=±5% resistance=100 package="0805 [SMD]"]
  D1 = Rectifier Diode [package="Melf DO-213 AA [SMD]"]
  R8/Heating_pad = Resistor [tolerance=±5% resistance=10 package="2512 [SMD]"]
  R4 = Resistor [tolerance=±5% resistance=100 package="0805 [SMD]"]
  Q3_2N2222A = TRANSISTOR_NPN [package=to-92]
  Q4_2N2222A = TRANSISTOR_NPN [package=to-92]
  R9 = Resistor [tolerance=±5% resistance=2k package="2512 [SMD]"]
  R10 = Resistor [tolerance=±5% resistance=2k package="2512 [SMD]"]
  Q5_2N2222A = TRANSISTOR_NPN [package=to-92]
  R11 = Resistor [tolerance=±5% resistance=5.1k package="2512 [SMD]"]
  L1_SOLENOIDE_LOCK = Solenoid
  D3 = Rectifier Diode [package="Melf DO-213 AA [SMD]"]
  Q5_TIP120 = TRANSISTOR_NPN [package=to-92]
  R12 = Resistor [tolerance=±5% resistance=470k package="2512 [SMD]"]
  S2 = Momentary Switch [package=tactile_switch_smd]
  DS1 = DS18B20 1-Wire Temperature Sensor [part_number=DS18B20]
  R14 = Resistor [tolerance=±5% resistance=4.7k package="0805 [SMD]"]
  S3 = TILT-SWITCH-SW-200D [package=reed_switch_plastic]
  R15 = Resistor [tolerance=±5% resistance=470 package="0805 [SMD]"]
  R16 = Resistor [tolerance=±5% resistance=470 package="0805 [SMD]"]
  U1 = PCF8574 [package="DIP16 [THT]"]
  U2 = LCD-16X2 [package=lcd-8x2]
  R17 = Photocell (LDR) [package=THT]
  R18 = Trimmer Potentiometer [maximum_resistance=10kΩ package=THT]
  R19 = Resistor [tolerance=±5% resistance=10k package="0805 [SMD]"]
  R20 = Trimmer Potentiometer [maximum_resistance=10kΩ package=THT]
  LED_4 = LEDs [package=led10mm]
  LED6 = LEDs [package=led10mm]
  R22 = Resistor [tolerance=±5% resistance=100 package="0805 [SMD]"]
  R23 = Resistor [tolerance=±5% resistance=100 package="0805 [SMD]"]
  Powerbank_INPUT_5V = BC9VPC [package=bc9vpc]
  U3 = Mini-360 DC-DC Buck converter [package=THT]
  D4 = Rectifier Diode [package="Melf DO-213 AA [SMD]"]
  INA5 = INA219 DC Current Sensor Breakout
  Part1 = Arduino Uno (Rev3) - ICSP
  INA7 = INA219 DC Current Sensor Breakout
  Part3 = I2C level shifter bidirectional

nets:
  N1: Raspberry_Pi_5_8GB.GPIO2, INA1.SDA, INA2.SDA, INA3.SDA, INA4.SDA, U1.SDA
  N2: Raspberry_Pi_5_8GB.GPIO3, INA1.SCL, INA2.SCL, INA3.SCL, INA4.SCL, U1.SCL
  N3: Raspberry_Pi_5_8GB.GPIO4, DS1.DQ, R14.Pin_0
  N4: Raspberry_Pi_5_8GB.GPIO10, MCP3008.Din, RFID.MOSI
  N5: Raspberry_Pi_5_8GB.GPIO9, MCP3008.Dout, RFID.MISO
  N6: Raspberry_Pi_5_8GB.GPIO11, MCP3008.CLK, RFID.SCK
  GND: Raspberry_Pi_5_8GB.GND, Powerbank_OUTPUT_5V.V-, 5V_TO_3V3.1, 5V_TO_3V3.4
  N7: Raspberry_Pi_5_8GB.GPIO5, U2.E
  N8: Raspberry_Pi_5_8GB.GPIO6, U2.RS
  N9: Raspberry_Pi_5_8GB.GPIO13, S3.2, R15.Pin_1
  N10: Raspberry_Pi_5_8GB.GPIO19, S2.3, R16.Pin_1
  N11: Raspberry_Pi_5_8GB.GPIO26, IR1.Data
  N12: Raspberry_Pi_5_8GB.GPIO21, R12.Pin_0
  N13: Raspberry_Pi_5_8GB.GPIO20, R11.Pin_0
  N14: Raspberry_Pi_5_8GB.GPIO16, R6.Pin_0
  N15: Raspberry_Pi_5_8GB.GPIO12, R5.Pin_0
  N16: Raspberry_Pi_5_8GB.GPIO7, RFID.SDA
  N17: Raspberry_Pi_5_8GB.GPIO8, MCP3008.CS/SHDN
  N18: Raspberry_Pi_5_8GB.GPIO25, R10.Pin_0
  N19: Raspberry_Pi_5_8GB.GPIO24, R9.Pin_0
  N20: Raspberry_Pi_5_8GB.GPIO15, Part3.LV4
  N21: Raspberry_Pi_5_8GB.GPIO14, Part3.LV1
  N22: MCP3008.CH0, R17.pin_0, R19.Pin_1
  N23: MCP3008.CH1, R18.wiper
  GND_2: MCP3008.DGND, MCP3008.AGND, IR1.GND, INA1.GND, RFID.RST, INA2.GND, INA3.GND, INA4.GND, Q2_SS8050.E, S2.1, DS1.GND, S3.1, U1.A0, U1.A1, U1.A2, U1.GND, U2.VSS, U2.R_W, U2.K, R17.pin_1, R18.leg2, R20.leg1, Part1.GND, INA7.GND, Part3.GND
  VCC: MCP3008.VREF, MCP3008.VDD, INA1.VCC, INA1.Vin+, RFID.3.3V, INA2.VCC, INA2.Vin+, INA3.VCC, INA4.VCC, 5V_TO_3V3.2, DS1.VDD, R14.Pin_1, R15.Pin_0, R16.Pin_0, R18.leg1, R19.Pin_0, LED_4.A, LED6.A, INA5.VCC, INA7.VCC, Part3.LV
  N24: IR1.Vs, INA3.Vin+, INA4.Vin+, 5V_TO_3V3.3, L1_SOLENOIDE_LOCK.pin1, D3.cathode, U2.VDD, U2.A, R20.leg2, INA7.Vin-, Part3.HV
  N25: Solar_panel.A, U3.IN-
  N26: Solar_panel.C, D4.anode
  N27: Powerbank_OUTPUT_5V.V+, INA7.Vin+
  N28: LED1.C, R1.Pin_0
  N29: LED1.A, LED2.A
  N30: LED2.C, R2.Pin_0
  N31: LED4.C, R3.Pin_0
  N32: LED4.A, LED_3.A, INA2.Vin-
  N33: LED_3.C, R4.Pin_0
  N34: M1.pin_1, D1.cathode
  N35: M1.pin_2, Q1_SS8050.C, D1.anode
  N36: INA4.Vin-, R7/Heating_pad.Pin_0, R8/Heating_pad.Pin_0
  N37: R7/Heating_pad.Pin_1, Q2_SS8050.C, R8/Heating_pad.Pin_1
  N38: Q1_SS8050.E, Q3_2N2222A.E, Q4_2N2222A.E, Q5_2N2222A.E, Q5_TIP120.E, INA5.GND
  N39: Q1_SS8050.B, R5.Pin_1
  N40: Q2_SS8050.B, R6.Pin_1
  N41: R1.Pin_1, R2.Pin_1, Q4_2N2222A.C
  N42: R3.Pin_1, R4.Pin_1, Q3_2N2222A.C
  N43: Q3_2N2222A.B, R10.Pin_1
  N44: Q4_2N2222A.B, R9.Pin_1
  N45: Q5_2N2222A.B, R11.Pin_1
  N46: Q5_2N2222A.C, R22.Pin_1, R23.Pin_1
  N47: L1_SOLENOIDE_LOCK.pin2, D3.anode, Q5_TIP120.C
  N48: Q5_TIP120.B, R12.Pin_1
  N49: U1.P0, U2.DB0
  N50: U1.P1, U2.DB1
  N51: U1.P2, U2.DB2
  N52: U1.P3, U2.DB3
  N53: U1.P4, U2.DB4
  N54: U1.P5, U2.DB5
  N55: U1.P6, U2.DB6
  N56: U1.P7, U2.DB7
  N57: U2.VO, R20.wiper
  N58: LED_4.C, R23.Pin_0
  N59: LED6.C, R22.Pin_0
  N60: Powerbank_INPUT_5V.V+, INA5.Vin-
  N61: Powerbank_INPUT_5V.V-, U3.OUT-
  N62: U3.IN+, D4.cathode
  N63: U3.OUT+, INA5.Vin+
  N64: INA5.SCL, Part1.A5/SCL, INA7.SCL
  N65: INA5.SDA, Part1.ICSP_MISO, INA7.SDA
  N66: Part1.D0/RX, Part3.HV1
  N67: Part1.D1/TX, Part3.HV4

custom parts:
  INA219 DC Current Sensor Breakout: INA DC Current Sensor Breakout
  RFID-RC522-v2: A simple China made RFID-RC522 Reader; do check the pin labels, as this is a MFRC522 based clone.
  Mini-360 DC-DC Buck converter: Mini-360 DC-DC Buck converter. Tiny buck step down voltage converter, input voltage 4.75 to 23V output 1 to 17V adjustable. Available from ebay and the like.
